// Logisim project 16_bitALU.circ as structural Verilog: 23 circuits, main circuit AU_RU
module add (
  input  [15:0] A,
  input  [15:0] B,
  output [15:0] \output 
);

  Adder #(.width(16)) adder_1 (.a(A), .b(B), .out(\output ));  // open: cin, cout
endmodule

module sub (
  input  [15:0] A,
  input  [15:0] B,
  output [15:0] out_3
);

  Subtractor #(.width(16)) subtractor_1 (.a(A), .b(B), .out(out_3));  // open: bin, bout
endmodule

module div (
  input  [15:0] A,
  input  [15:0] B,
  output [15:0] \output 
);

  Divider #(.width(16)) divider_1 (.a(A), .b(B), .out(\output ));  // open: upper, rem
endmodule

module bitwiseAND (
  input  [15:0] A,
  input  [15:0] B,
  output [15:0] \output 
);

  assign \output  = A & B;  // AND_Gate and_1, 16 bits wide
endmodule

module bitwiseOR (
  input  [15:0] A,
  input  [15:0] B,
  output [15:0] OUTPUT
);

  assign OUTPUT = A | B;  // OR_Gate or_1, 16 bits wide
endmodule

module bitwiseXOR (
  input  [15:0] A,
  input  [15:0] B,
  output [15:0] \output 
);

  assign \output  = A ^ B;  // XOR_Gate xor_1, 16 bits wide
endmodule

module mult (
  input  [15:0] A,
  input  [15:0] B,
  output [15:0] \output 
);

  Multiplier #(.width(16)) multiplier_1 (.a(A), .b(B), .out(\output ));  // open: cin, cout
endmodule

module logicLEFTA (
  input  [15:0] A,
  input  [3:0] distance,
  output [15:0] \output 
);

  Shifter #(.width(16)) shifter_1 (.in(A), .\dist (distance), .out(\output ));
endmodule

module logicRIGHTA (
  input  [15:0] A,
  input  [3:0] distance,
  output [15:0] \output 
);

  Shifter #(.shift("lr"), .width(16)) shifter_1 (.in(A), .\dist (distance), .out(\output ));
endmodule

module logicLEFTB (
  input  [15:0] B,
  input  [3:0] distance,
  output [15:0] \output 
);

  Shifter #(.width(16)) shifter_1 (.in(B), .\dist (distance), .out(\output ));
endmodule

module logicRIGHTB (
  input  [15:0] B,
  input  [3:0] distance,
  output [15:0] \output 
);

  Shifter #(.shift("lr"), .width(16)) shifter_1 (.in(B), .\dist (distance), .out(\output ));
endmodule

module mod (
  input  [15:0] A,
  input  [15:0] B,
  output [15:0] rem
);

  Divider #(.width(16)) divider_1 (.a(A), .b(B), .rem(rem));  // open: out, upper
endmodule

module twosComplimentA (
  input  [15:0] A,
  output [15:0] \output 
);

  Negator #(.width(16)) negator_1 (.in(A), .out(\output ));
endmodule

module twosComplimentB (
  input  [15:0] B,
  output [15:0] \output 
);

  Negator #(.width(16)) negator_1 (.in(B), .out(\output ));
endmodule

module greaterThan (
  input  [15:0] A,
  input  [15:0] B,
  output \output 
);

  Comparator #(.width(16)) comparator_1 (.a(A), .b(B), .gt(\output ));  // open: eq, lt
endmodule

module lessThan (
  input  [15:0] A,
  input  [15:0] B,
  output \output 
);

  Comparator #(.width(16)) comparator_1 (.a(A), .b(B), .lt(\output ));  // open: gt, eq
endmodule

module equal (
  input  [15:0] A,
  input  [15:0] B,
  output \output 
);

  Comparator #(.width(16)) comparator_1 (.a(A), .b(B), .eq(\output ));  // open: gt, lt
endmodule

module notEqual (
  input  [15:0] A,
  input  [15:0] B,
  output out_3
);

  wire comparator_1_gt, comparator_1_lt;

  Comparator #(.width(16)) comparator_1 (.a(A), .b(B), .gt(comparator_1_gt), .lt(comparator_1_lt));  // open: eq
  or or_1 (out_3, comparator_1_gt, comparator_1_lt);
endmodule

module lessOrEqual (
  input  [15:0] A,
  input  [15:0] B,
  output out_3
);

  wire comparator_1_eq, comparator_1_lt;

  Comparator #(.width(16)) comparator_1 (.a(A), .b(B), .eq(comparator_1_eq), .lt(comparator_1_lt));  // open: gt
  or or_1 (out_3, comparator_1_eq, comparator_1_lt);
endmodule

module greaterOrEqual (
  input  [15:0] A,
  input  [15:0] B,
  output out_3
);

  wire comparator_1_eq, comparator_1_gt;

  Comparator #(.width(16)) comparator_1 (.a(A), .b(B), .gt(comparator_1_gt), .eq(comparator_1_eq));  // open: lt
  or or_1 (out_3, comparator_1_gt, comparator_1_eq);
endmodule

module ALU (
  input  [15:0] A,
  input  [15:0] B,
  input  [4:0] AUC,
  input  AUENABLE,
  output [15:0] AUoutput
);

  wire [15:0] add_1_output, bitwiseand_1_output, bitwiseor_1_output, bitwisexor_1_output, div_1_output,
       logiclefta_1_output, logicleftb_1_output, logicrighta_1_output, logicrightb_1_output, mod_1_rem,
       mult_1_output, sub_1_out_3, twoscomplimenta_1_output, twoscomplimentb_1_output;

  add add_1 (.A(A), .B(B), .\output (add_1_output));
  bitwiseAND bitwiseand_1 (.A(A), .B(B), .\output (bitwiseand_1_output));
  bitwiseOR bitwiseor_1 (.A(A), .B(B), .OUTPUT(bitwiseor_1_output));
  bitwiseXOR bitwisexor_1 (.A(A), .B(B), .\output (bitwisexor_1_output));
  div div_1 (.A(A), .B(B), .\output (div_1_output));
  mod mod_1 (.A(A), .B(B), .rem(mod_1_rem));
  mult mult_1 (.A(A), .B(B), .\output (mult_1_output));
  sub sub_1 (.A(A), .B(B), .out_3(sub_1_out_3));
  logicLEFTA logiclefta_1 (.A(A), .distance(B[3:0]), .\output (logiclefta_1_output));
  logicRIGHTA logicrighta_1 (.A(A), .distance(B[3:0]), .\output (logicrighta_1_output));
  logicLEFTB logicleftb_1 (.B(B), .distance(B[3:0]), .\output (logicleftb_1_output));
  logicRIGHTB logicrightb_1 (.B(B), .distance(B[3:0]), .\output (logicrightb_1_output));
  twosComplimentA twoscomplimenta_1 (.A(A), .\output (twoscomplimenta_1_output));
  twosComplimentB twoscomplimentb_1 (.B(B), .\output (twoscomplimentb_1_output));
  Multiplexer #(.enable("true"), .select(5), .width(16)) multiplexer_1 (
    .in0(add_1_output), .in1(bitwiseand_1_output), .in2(bitwiseor_1_output), .in3(bitwisexor_1_output),
    .in4(div_1_output), .in5(mod_1_rem), .in6(mult_1_output), .in7(sub_1_out_3), .in8(logiclefta_1_output),
    .in9(logicrighta_1_output), .in10(logicleftb_1_output), .in11(logicrightb_1_output),
    .in12(twoscomplimenta_1_output), .in13(twoscomplimentb_1_output), .in14({16{1'b0}}), .in15({16{1'b0}}),
    .in16({16{1'b0}}), .in17({16{1'b0}}), .in18({16{1'b0}}), .in19({16{1'b0}}), .in20({16{1'b0}}),
    .in21({16{1'b0}}), .in22({16{1'b0}}), .in23({16{1'b0}}), .in24({16{1'b0}}), .in25({16{1'b0}}),
    .in26({16{1'b0}}), .in27({16{1'b0}}), .in28({16{1'b0}}), .in29({16{1'b0}}), .in30({16{1'b0}}),
    .in31({16{1'b0}}), .out(AUoutput), .sel(AUC), .en(AUENABLE));

  // Notes on the sheet:
  //   add
  //   and
  //   or
  //   xor
  //   div
  //   mod
  //   mult
  //   sub
  //   SLA
  //   SRA
  //   SLB
  //   SRB
  //   TCsA
  //   TCsB
endmodule

module RLU (
  input  RUENABLE,
  input  [15:0] A,
  input  [2:0] RUSEL,
  input  [15:0] B,
  output [15:0] RUOUT
);

  wire equal_1_output, greaterorequal_1_out_3, greaterthan_1_output, lessorequal_1_out_3, lessthan_1_output,
       multiplexer_1_out, notequal_1_out_3;

  greaterThan greaterthan_1 (.A(A), .B(B), .\output (greaterthan_1_output));
  lessThan lessthan_1 (.A(A), .B(B), .\output (lessthan_1_output));
  equal equal_1 (.A(A), .B(B), .\output (equal_1_output));
  notEqual notequal_1 (.A(A), .B(B), .out_3(notequal_1_out_3));
  lessOrEqual lessorequal_1 (.A(A), .B(B), .out_3(lessorequal_1_out_3));
  greaterOrEqual greaterorequal_1 (.A(A), .B(B), .out_3(greaterorequal_1_out_3));
  Multiplexer #(.enable("true"), .select(3)) multiplexer_1 (
    .in0(greaterthan_1_output), .in1(lessthan_1_output), .in2(equal_1_output), .in3(notequal_1_out_3),
    .in4(lessorequal_1_out_3), .in5(greaterorequal_1_out_3), .in6(1'b0), .in7(1'b0), .out(multiplexer_1_out),
    .sel(RUSEL), .en(RUENABLE));
  assign RUOUT = {{15{1'b0}}, multiplexer_1_out};  // Bit_Extender bit_extender_1

  // Notes on the sheet:
  //   LT
  //   Equal
  //   NotEqual
  //   LEQ
  //   GEQ
endmodule

module AU_RU (
  input  AOE,
  input  [15:0] A,
  input  [4:0] AUSEL,
  input  [15:0] B,
  input  AUENABLE,
  input  ROE,
  input  [2:0] RUSEL,
  input  RUENABLE,
  output [15:0] ADOUT,
  output [15:0] AUOUTPUT,
  output [15:0] RDOUT,
  output [15:0] RUOUTPUT
);

  ALU alu_1 (.AUC(AUSEL), .AUENABLE(AUENABLE), .B(B), .A(A), .AUoutput(AUOUTPUT));
  RLU rlu_1 (.A(A), .RUSEL(RUSEL), .RUENABLE(RUENABLE), .B(B), .RUOUT(RUOUTPUT));
  assign ADOUT = AOE ? AUOUTPUT : 16'bz;  // Controlled_Buffer controlled_buffer_1
  assign RDOUT = ROE ? RUOUTPUT : 16'bz;  // Controlled_Buffer controlled_buffer_2
endmodule
