// Logisim project CPU.circ as structural Verilog: 3 circuits, main circuit main
module main (
  input  [15:0] in_1,
  input  in_2,
  input  OPEnable,
  input  AUE,
  input  rOE,
  output [7:0] out_6,
  output [7:0] out_7,
  output [15:0] out_8,
  output [15:0] out_9,
  output [15:0] out_10,
  output [15:0] out_11,
  output [15:0] out_12,
  output [15:0] out_13,
  output [15:0] out_14
);

  wire clock_1_out, cu_1_c0, cu_1_c1, cu_1_c2, cu_1_c3, cu_1_c4, cu_1_c5, cu_1_c6, cu_1_c7, cu_1_c8, cu_1_c9,
       cu_1_c10, cu_1_c11, cu_1_c12, cu_1_c13, cu_1_c14, cu_1_c15;
  wire [2:0] Step_Counter_q;
  wire [3:0] bcd_to_7_segment_decoder_16_p1, bcd_to_7_segment_decoder_22_p1, bitselector_2_out,
       n7_segment_display_1_p1, n7_segment_display_1_p2, n7_segment_display_2_p1, n7_segment_display_2_p2,
       n7_segment_display_3_p1, n7_segment_display_3_p2, n7_segment_display_4_p2, n7_segment_display_5_p2,
       n7_segment_display_6_p2, n7_segment_display_17_p1, n7_segment_display_17_p2, n7_segment_display_18_p2,
       n7_segment_display_19_p2, n7_segment_display_20_p2, seven_segment_display_1_oneth,
       seven_segment_display_1_tenth, seven_segment_display_2_oneth, seven_segment_display_2_tenth,
       seven_segment_display_3_oneth, seven_segment_display_3_tenth;
  wire [7:0] bitselector_1_out, MAR_dout;
  wire [15:0] au_ru_1_adout, bit_extender_1_out, bit_extender_2_out, Instruction_Register_dout, ram_1_dout;

  // BCD_to_7_Segment_decoder bcd_to_7_segment_decoder_1: pin names not known
  // _7_Segment_Display 7_segment_display_1: pin names not known; wires that end beside it: n7_segment_display_1_p1, n7_segment_display_1_p2
  // BCD_to_7_Segment_decoder bcd_to_7_segment_decoder_2: pin names not known
  // _7_Segment_Display 7_segment_display_2: pin names not known; wires that end beside it: n7_segment_display_2_p1, n7_segment_display_2_p2
  // BCD_to_7_Segment_decoder bcd_to_7_segment_decoder_3: pin names not known
  // _7_Segment_Display 7_segment_display_3: pin names not known; wires that end beside it: n7_segment_display_3_p1, n7_segment_display_3_p2
  // BCD_to_7_Segment_decoder bcd_to_7_segment_decoder_4: pin names not known
  // _7_Segment_Display 7_segment_display_4: pin names not known; wires that end beside it: n7_segment_display_1_p2, n7_segment_display_4_p2
  seven_segment_display seven_segment_display_1 (
    .Din(out_10), .HUNDREDTH(n7_segment_display_4_p2), .TENTH(seven_segment_display_1_tenth),
    .ONETH(seven_segment_display_1_oneth), .TEN_THOUSAND(n7_segment_display_1_p1),
    .THOUSANDTH(n7_segment_display_1_p2));
  // BCD_to_7_Segment_decoder bcd_to_7_segment_decoder_5: pin names not known
  // _7_Segment_Display 7_segment_display_5: pin names not known; wires that end beside it: n7_segment_display_2_p2, n7_segment_display_5_p2
  seven_segment_display seven_segment_display_2 (
    .Din(out_11), .HUNDREDTH(n7_segment_display_5_p2), .TENTH(seven_segment_display_2_tenth),
    .ONETH(seven_segment_display_2_oneth), .TEN_THOUSAND(n7_segment_display_2_p1),
    .THOUSANDTH(n7_segment_display_2_p2));
  // BCD_to_7_Segment_decoder bcd_to_7_segment_decoder_6: pin names not known
  // _7_Segment_Display 7_segment_display_6: pin names not known; wires that end beside it: n7_segment_display_3_p2, n7_segment_display_6_p2
  seven_segment_display seven_segment_display_3 (
    .Din(out_14), .HUNDREDTH(n7_segment_display_6_p2), .TENTH(seven_segment_display_3_tenth),
    .ONETH(seven_segment_display_3_oneth), .TEN_THOUSAND(n7_segment_display_3_p1),
    .THOUSANDTH(n7_segment_display_3_p2));
  // BCD_to_7_Segment_decoder bcd_to_7_segment_decoder_7: pin names not known
  // BCD_to_7_Segment_decoder bcd_to_7_segment_decoder_8: pin names not known
  // _7_Segment_Display 7_segment_display_7: pin names not known; wires that end beside it: n7_segment_display_4_p2, seven_segment_display_1_tenth
  // _7_Segment_Display 7_segment_display_8: pin names not known; wires that end beside it: seven_segment_display_1_tenth, seven_segment_display_1_oneth
  // BCD_to_7_Segment_decoder bcd_to_7_segment_decoder_9: pin names not known
  // BCD_to_7_Segment_decoder bcd_to_7_segment_decoder_10: pin names not known
  // _7_Segment_Display 7_segment_display_9: pin names not known; wires that end beside it: n7_segment_display_5_p2, seven_segment_display_2_tenth
  // _7_Segment_Display 7_segment_display_10: pin names not known; wires that end beside it: seven_segment_display_2_tenth, seven_segment_display_2_oneth
  // BCD_to_7_Segment_decoder bcd_to_7_segment_decoder_11: pin names not known
  // BCD_to_7_Segment_decoder bcd_to_7_segment_decoder_12: pin names not known
  // _7_Segment_Display 7_segment_display_11: pin names not known; wires that end beside it: n7_segment_display_6_p2, seven_segment_display_3_tenth
  // _7_Segment_Display 7_segment_display_12: pin names not known; wires that end beside it: seven_segment_display_3_tenth, seven_segment_display_3_oneth
  // BCD_to_7_Segment_decoder bcd_to_7_segment_decoder_13: pin names not known
  _7_Segment_Display u_7_segment_display_13 ();  // open: g, f, a, b, e, d, c, dp
  // BCD_to_7_Segment_decoder bcd_to_7_segment_decoder_14: pin names not known
  _7_Segment_Display u_7_segment_display_14 ();  // open: g, f, a, b, e, d, c, dp
  // BCD_to_7_Segment_decoder bcd_to_7_segment_decoder_15: pin names not known
  _7_Segment_Display u_7_segment_display_15 ();  // open: g, f, a, b, e, d, c, dp
  Clock clock_1 (.out(clock_1_out));
  // BCD_to_7_Segment_decoder bcd_to_7_segment_decoder_16: pin names not known; wires that end beside it: bcd_to_7_segment_decoder_16_p1
  _7_Segment_Display u_7_segment_display_16 ();  // open: g, f, a, b, e, d, c, dp
  seven_segment_display seven_segment_display_4 (
    .Din(bit_extender_1_out), .ONETH(bcd_to_7_segment_decoder_16_p1));  // open: HUNDREDTH, TENTH, TEN_THOUSAND, THOUSANDTH
  assign bit_extender_1_out = {{8{1'b0}}, out_7};  // Bit_Extender bit_extender_1
  Counter #(.max('h3)) PC (
    .D(bitselector_1_out), .count(cu_1_c1), .Q(out_7), .clk(clock_1_out));  // open: load, carry, up, clr
  Sixteen_bit_register Instruction_Register (
    .Din(au_ru_1_adout), .OE(cu_1_c8), .Clock(clock_1_out), .WE(cu_1_c7), .Dout(Instruction_Register_dout),
    .Stored_bit(out_8));  // open: Reset
  Sixteen_bit_register Register_A (
    .Din(au_ru_1_adout), .Clock(clock_1_out), .WE(cu_1_c12), .Stored_bit(out_10));  // open: OE, Reset, Dout
  Sixteen_bit_register sixteen_bit_register_1 (
    .Din(au_ru_1_adout), .Clock(clock_1_out), .WE(cu_1_c13), .Stored_bit(out_14));  // open: OE, Reset, Dout
  BitSelector #(.group(8), .width(16)) bitselector_1 (
    .in(Instruction_Register_dout), .out(bitselector_1_out), .sel(1'b0));
  AU_RU au_ru_1 (
    .A(out_10), .B(out_14), .AUENABLE(AUE), .AOE(cu_1_c11), .ROE(rOE), .ADOUT(au_ru_1_adout),
    .AUOUTPUT(out_11), .RDOUT(au_ru_1_adout), .RUOUTPUT(out_12));  // open: AUSEL, RUSEL, RUENABLE
  assign bitselector_1_out = cu_1_c0 ? out_7 : 8'bz;  // Controlled_Buffer controlled_buffer_1
  LED led_1 (.in(au_ru_1_adout[15]));
  LED led_2 (.in(au_ru_1_adout[14]));
  LED led_3 (.in(au_ru_1_adout[13]));
  LED led_4 (.in(au_ru_1_adout[12]));
  LED led_5 (.in(au_ru_1_adout[11]));
  LED led_6 (.in(au_ru_1_adout[10]));
  assign au_ru_1_adout = in_2 ? in_1 : 16'bz;  // Controlled_Buffer controlled_buffer_2
  LED led_7 (.in(au_ru_1_adout[9]));
  LED led_8 (.in(au_ru_1_adout[8]));
  LED led_9 (.in(au_ru_1_adout[7]));
  LED led_10 (.in(au_ru_1_adout[6]));
  LED led_11 (.in(au_ru_1_adout[5]));
  LED led_12 (.in(au_ru_1_adout[4]));
  LED led_13 (.in(au_ru_1_adout[3]));
  LED led_14 (.in(au_ru_1_adout[2]));
  LED led_15 (.in(au_ru_1_adout[1]));
  LED led_16 (.in(au_ru_1_adout[0]));
  assign au_ru_1_adout = cu_1_c5 ? out_9 : 16'bz;  // Controlled_Buffer controlled_buffer_3
  Eight_bit_register MAR (
    .Din(bitselector_1_out), .OE(cu_1_c10), .Clock(clock_1_out), .WE(cu_1_c9), .Stored_bit(out_6),
    .Dout(MAR_dout));  // open: Reset
  Sixteen_bit_register MBR (
    .Din(au_ru_1_adout), .OE(cu_1_c6), .Clock(clock_1_out), .WE(cu_1_c4), .Dout(au_ru_1_adout),
    .Stored_bit(out_9));  // open: Reset
  Sixteen_bit_register Output_Register (
    .Din(au_ru_1_adout), .OE(cu_1_c14), .Clock(clock_1_out), .WE(cu_1_c15), .Dout(au_ru_1_adout),
    .Stored_bit(out_13));  // open: Reset
  LED led_17 (.in(au_ru_1_adout[15]));
  LED led_18 (.in(au_ru_1_adout[14]));
  LED led_19 (.in(au_ru_1_adout[13]));
  // BCD_to_7_Segment_decoder bcd_to_7_segment_decoder_17: pin names not known
  // BCD_to_7_Segment_decoder bcd_to_7_segment_decoder_18: pin names not known
  // _7_Segment_Display 7_segment_display_17: pin names not known; wires that end beside it: n7_segment_display_17_p1, n7_segment_display_17_p2
  // _7_Segment_Display 7_segment_display_18: pin names not known; wires that end beside it: n7_segment_display_17_p2, n7_segment_display_18_p2
  LED led_20 (.in(au_ru_1_adout[12]));
  LED led_21 (.in(au_ru_1_adout[11]));
  LED led_22 (.in(au_ru_1_adout[10]));
  LED led_23 (.in(au_ru_1_adout[9]));
  // BCD_to_7_Segment_decoder bcd_to_7_segment_decoder_19: pin names not known
  // BCD_to_7_Segment_decoder bcd_to_7_segment_decoder_20: pin names not known
  // _7_Segment_Display 7_segment_display_19: pin names not known; wires that end beside it: n7_segment_display_18_p2, n7_segment_display_19_p2
  // _7_Segment_Display 7_segment_display_20: pin names not known; wires that end beside it: n7_segment_display_19_p2, n7_segment_display_20_p2
  seven_segment_display seven_segment_display_5 (
    .Din(out_13), .HUNDREDTH(n7_segment_display_18_p2), .TENTH(n7_segment_display_19_p2),
    .ONETH(n7_segment_display_20_p2), .TEN_THOUSAND(n7_segment_display_17_p1),
    .THOUSANDTH(n7_segment_display_17_p2));
  LED led_24 (.in(au_ru_1_adout[8]));
  LED led_25 (.in(au_ru_1_adout[7]));
  LED led_26 (.in(au_ru_1_adout[6]));
  LED led_27 (.in(au_ru_1_adout[5]));
  // BCD_to_7_Segment_decoder bcd_to_7_segment_decoder_21: pin names not known
  _7_Segment_Display u_7_segment_display_21 ();  // open: g, f, a, b, e, d, c, dp
  LED led_28 (.in(au_ru_1_adout[4]));
  LED led_29 (.in(au_ru_1_adout[3]));
  LED led_30 (.in(au_ru_1_adout[2]));
  LED led_31 (.in(au_ru_1_adout[1]));
  LED led_32 (.in(au_ru_1_adout[0]));
  RAM #(.dataWidth(16), .enables("line"), .\type ("nonvolatile")) ram_1 (
    .addr(MAR_dout), .we(cu_1_c2), .clk(clock_1_out), .din(au_ru_1_adout), .dout(ram_1_dout));
  assign au_ru_1_adout = cu_1_c3 ? ram_1_dout : 16'bz;  // Controlled_Buffer controlled_buffer_4
  Counter #(.max('h5), .width(3)) Step_Counter (
    .Q(Step_Counter_q), .clk(clock_1_out));  // open: load, D, count, carry, up, clr
  BitSelector #(.group(4), .width(16)) bitselector_2 (.in(out_8), .out(bitselector_2_out), .sel(2'b01));
  assign bit_extender_2_out = {{13{1'b0}}, Step_Counter_q};  // Bit_Extender bit_extender_2
  // BCD_to_7_Segment_decoder bcd_to_7_segment_decoder_22: pin names not known; wires that end beside it: bcd_to_7_segment_decoder_22_p1
  _7_Segment_Display u_7_segment_display_22 ();  // open: g, f, a, b, e, d, c, dp
  seven_segment_display seven_segment_display_6 (
    .Din(bit_extender_2_out), .ONETH(bcd_to_7_segment_decoder_22_p1));  // open: HUNDREDTH, TENTH, TEN_THOUSAND, THOUSANDTH
  CU cu_1 (
    .OPC1(bitselector_2_out[1]), .OPC0(bitselector_2_out[0]), .SC2(Step_Counter_q[2]),
    .SC1(Step_Counter_q[1]), .SC0(Step_Counter_q[0]), .OPC3(bitselector_2_out[3]),
    .OPC2(bitselector_2_out[2]), .C2(cu_1_c2), .C3(cu_1_c3), .C4(cu_1_c4), .C5(cu_1_c5), .C6(cu_1_c6),
    .C7(cu_1_c7), .C8(cu_1_c8), .C9(cu_1_c9), .C10(cu_1_c10), .C11(cu_1_c11), .C12(cu_1_c12), .C13(cu_1_c13),
    .C14(cu_1_c14), .C15(cu_1_c15), .C0(cu_1_c0), .C1(cu_1_c1));
endmodule

module CU (
  input  OPC3,
  input  OPC2,
  input  OPC1,
  input  OPC0,
  input  SC2,
  input  SC1,
  input  SC0,
  output C0,
  output C1,
  output C2,
  output C3,
  output C4,
  output C5,
  output C6,
  output C7,
  output C8,
  output C9,
  output C10,
  output C11,
  output C12,
  output C13,
  output C14,
  output C15
);

  wire and_4_out, and_5_out, and_6_out, and_7_out, and_8_out, and_9_out, and_10_out, and_13_out, and_14_out,
       and_15_out, and_16_out, and_17_out, and_18_out, and_19_out, not_1_out, not_2_out, not_3_out,
       not_4_out, not_5_out;

  not not_1 (not_1_out, OPC1);
  not not_2 (not_2_out, OPC0);
  not not_3 (not_3_out, SC2);
  not not_4 (not_4_out, SC1);
  not not_5 (not_5_out, SC0);
  and and_1 (C0, not_3_out, not_4_out, not_5_out);
  and and_2 (C1, not_3_out, not_4_out, SC0);
  and and_3 (C2, OPC1, SC2);
  and and_4 (and_4_out, not_3_out, not_4_out, SC0);
  and and_5 (and_5_out, not_1_out, SC2, not_5_out);
  and and_6 (and_6_out, not_3_out, not_4_out, SC0);
  and and_7 (and_7_out, OPC1, OPC0, SC0);
  and and_8 (and_8_out, not_1_out, SC2, not_5_out);
  and and_9 (and_9_out, SC1, not_5_out);
  and and_10 (and_10_out, SC2, SC0);
  and and_11 (C6, OPC1, SC2);
  and and_12 (C7, SC1, not_5_out);
  and and_13 (and_13_out, not_1_out, SC1, SC0);
  and and_14 (and_14_out, OPC0, SC1, SC0);
  and and_15 (and_15_out, not_3_out, not_4_out, not_5_out);
  and and_16 (and_16_out, not_1_out, SC1, SC0);
  and and_17 (and_17_out, OPC0, SC1, SC0);
  and and_18 (and_18_out, not_3_out, not_4_out, SC0);
  and and_19 (and_19_out, SC2, not_5_out);
  and and_20 (C11, OPC1, not_2_out, SC1, SC0);
  and and_21 (C12, not_2_out, SC2, SC0);
  and and_22 (C13, OPC0, SC2, SC0);
  and and_23 (C14, OPC1, OPC0, SC1, SC0);
  and and_24 (C15, OPC1, not_2_out, SC1, SC0);
  or or_1 (C3, and_4_out, and_5_out);
  or or_2 (C4, and_6_out, and_7_out, and_8_out);
  or or_3 (C5, and_9_out, and_10_out);
  or or_4 (C8, and_13_out, and_14_out);
  or or_5 (C9, and_15_out, and_16_out, and_17_out);
  or or_6 (C10, and_18_out, and_19_out);
endmodule

module try (
  input  [6:0] in_1,
  output [15:0] out_2
);

  CU cu_1 (
    .OPC1(in_1[2]), .OPC0(in_1[3]), .SC2(in_1[4]), .SC1(in_1[5]), .SC0(in_1[6]), .OPC3(in_1[0]),
    .OPC2(in_1[1]), .C2(out_2[2]), .C3(out_2[3]), .C4(out_2[4]), .C5(out_2[5]), .C6(out_2[6]), .C7(out_2[7]),
    .C8(out_2[8]), .C9(out_2[9]), .C10(out_2[10]), .C11(out_2[11]), .C12(out_2[12]), .C13(out_2[13]),
    .C14(out_2[14]), .C15(out_2[15]), .C0(out_2[0]), .C1(out_2[1]));
endmodule
