// Logisim project Registers.circ as structural Verilog: 3 circuits, main circuit One_bit_register
module One_bit_register (
  input  WriteENable,
  input  Clock,
  input  Din,
  input  OutputEnable,
  input  Reset,
  output Dout,
  output Stored_bit
);

  wire and_1_out, and_2_out, not_1_out, or_1_out;

  not not_1 (not_1_out, WriteENable);
  and and_1 (and_1_out, Stored_bit, not_1_out);
  and and_2 (and_2_out, WriteENable, Din);
  or or_1 (or_1_out, and_1_out, and_2_out);
  D_Flip_Flop d_ff_1 (.D(or_1_out), .clk(Clock), .Q(Stored_bit), .reset(Reset));  // open: Qn, preset
  assign Dout = OutputEnable ? Stored_bit : 1'bz;  // Controlled_Buffer controlled_buffer_1
endmodule

module Eight_bit_register (
  input  [7:0] Din,
  input  WE,
  input  OE,
  input  Reset,
  input  Clock,
  output [7:0] Dout,
  output [7:0] Stored_bit
);

  One_bit_register one_bit_register_1 (
    .WriteENable(WE), .Din(Din[7]), .OutputEnable(OE), .Reset(Reset), .Clock(Clock), .Dout(Dout[7]),
    .Stored_bit(Stored_bit[7]));
  One_bit_register one_bit_register_2 (
    .WriteENable(WE), .Din(Din[6]), .OutputEnable(OE), .Reset(Reset), .Clock(Clock), .Dout(Dout[6]),
    .Stored_bit(Stored_bit[6]));
  One_bit_register one_bit_register_3 (
    .WriteENable(WE), .Din(Din[5]), .OutputEnable(OE), .Reset(Reset), .Clock(Clock), .Dout(Dout[5]),
    .Stored_bit(Stored_bit[5]));
  One_bit_register one_bit_register_4 (
    .WriteENable(WE), .Din(Din[4]), .OutputEnable(OE), .Reset(Reset), .Clock(Clock), .Dout(Dout[4]),
    .Stored_bit(Stored_bit[4]));
  One_bit_register one_bit_register_5 (
    .WriteENable(WE), .Din(Din[3]), .OutputEnable(OE), .Reset(Reset), .Clock(Clock), .Dout(Dout[3]),
    .Stored_bit(Stored_bit[3]));
  One_bit_register one_bit_register_6 (
    .WriteENable(WE), .Din(Din[2]), .OutputEnable(OE), .Reset(Reset), .Clock(Clock), .Dout(Dout[2]),
    .Stored_bit(Stored_bit[2]));
  One_bit_register one_bit_register_7 (
    .WriteENable(WE), .Din(Din[1]), .OutputEnable(OE), .Reset(Reset), .Clock(Clock), .Dout(Dout[1]),
    .Stored_bit(Stored_bit[1]));
  One_bit_register one_bit_register_8 (
    .WriteENable(WE), .Din(Din[0]), .OutputEnable(OE), .Reset(Reset), .Clock(Clock), .Dout(Dout[0]),
    .Stored_bit(Stored_bit[0]));
endmodule

module Sixteen_bit_register (
  input  [15:0] Din,
  input  WE,
  input  OE,
  input  Reset,
  input  Clock,
  output [15:0] Dout,
  output [15:0] Stored_bit
);

  Eight_bit_register eight_bit_register_1 (
    .Din(Din[15:8]), .OE(OE), .Reset(Reset), .Clock(Clock), .WE(WE), .Stored_bit(Stored_bit[15:8]),
    .Dout(Dout[15:8]));
  Eight_bit_register eight_bit_register_2 (
    .Din(Din[7:0]), .OE(OE), .Reset(Reset), .Clock(Clock), .WE(WE), .Stored_bit(Stored_bit[7:0]),
    .Dout(Dout[7:0]));
endmodule
