// Logisim project Decimaldecoder.circ as structural Verilog: 1 circuit, main circuit seven_segment_display
module seven_segment_display (
  input  [15:0] Din,
  output [3:0] THOUSANDTH,
  output [3:0] TEN_THOUSAND,
  output [3:0] HUNDREDTH,
  output [3:0] TENTH,
  output [3:0] ONETH
);

  wire [15:0] divider_1_out, divider_1_rem, multiplexer_1_out, negator_1_out;

  Negator #(.width(16)) negator_1 (.in(Din), .out(negator_1_out));
  Multiplexer #(.width(16)) multiplexer_1 (.in0(Din), .in1(negator_1_out), .out(multiplexer_1_out), .sel(Din[15]));
  Divider #(.width(16)) divider_1 (
    .a(multiplexer_1_out), .b(16'h3e8), .out(divider_1_out), .rem(divider_1_rem));  // open: upper
  // Binary_to_BCD_converter #(.binvalue(13)) binary_to_bcd_converter_1: pin names not known; wires that end beside it: divider_1_out[12:0], TEN_THOUSAND
  // Binary_to_BCD_converter #(.binvalue(13)) binary_to_bcd_converter_2: pin names not known; wires that end beside it: THOUSANDTH, divider_1_rem[12:0], HUNDREDTH, TENTH, ONETH
endmodule
